// Logisim project labo_alu_etu.circ as structural Verilog: 9 circuits, main circuit ALU_MAXV
module ALU_MAXV (
  input  [3:0] a_i,
  input  [3:0] b_i,
  output [3:0] c_o,
  output erreur_o
);

  wire [5:0] opcode_i_sw6;

  DipSwitch opcode_i (
    .sw1(opcode_i_sw6[5]), .sw2(opcode_i_sw6[4]), .sw3(opcode_i_sw6[3]), .sw4(opcode_i_sw6[2]),
    .sw5(opcode_i_sw6[1]), .sw6(opcode_i_sw6[0]));  // open: sw7, sw8
  ALU_Top alu_inst (.a_i(a_i), .b_i(b_i), .op_i(opcode_i_sw6), .c_o(c_o), .erreur_o(erreur_o));

  // Notes on the sheet:
  //   Attention, votre version de Logisim
  //   ne contient pas de tracker. Si vous
  //   enregistrez votre projet, toutes les
  //   informations du tracker seront
  //   définitivement effacées.
endmodule

module ALU_Top (
  input  [3:0] a_i,
  input  [3:0] b_i,
  input  [5:0] op_i,
  output [3:0] c_o,
  output erreur_o
);

  wire alu_addsub_1_c_o, alu_addsub_1_negative_o, alu_addsub_1_zero_o, and_1_out, and_2_out, and_3_out,
       and_4_out, and_5_out, and_6_out, not_1_out, not_2_out, not_3_out, not_4_out, not_5_out, or_1_out,
       overflow_o;
  wire [3:0] alu_addsub_1_r_o, alu_comp_1_cmp_o, alu_custom_1_s_o, alu_unitlogic_1_f_o;

  not not_1 (not_1_out, op_i[5]);
  not not_2 (not_2_out, op_i[3]);
  not not_3 (not_3_out, op_i[5]);
  and and_1 (and_1_out, op_i[3], op_i[4], not_1_out);
  ALU_Custom alu_custom_1 (.a_i(a_i), .s_o(alu_custom_1_s_o));
  and and_2 (and_2_out, not_2_out, op_i[4], not_3_out);
  and and_3 (and_3_out, op_i[2], op_i[1], op_i[0]);
  or or_1 (or_1_out, and_3_out, and_4_out);
  and and_4 (and_4_out, ~op_i[2], ~op_i[1], ~op_i[0]);  // AND_Gate
  ALU_AddSub alu_addsub_1 (
    .op3_i(op_i[3]), .a_i(a_i), .b_i(b_i), .op2_i(op_i[2]), .zero_o(alu_addsub_1_zero_o),
    .r_o(alu_addsub_1_r_o), .Negative_o(alu_addsub_1_negative_o), .c_o(alu_addsub_1_c_o),
    .overflow_o(overflow_o));
  ALU_Comp alu_comp_1 (
    .Negative_i(alu_addsub_1_negative_o), .carry_i(alu_addsub_1_zero_o), .zero_i(alu_addsub_1_c_o),
    .opcode_i(op_i), .cmp_o(alu_comp_1_cmp_o));
  ALU_UnitLogic alu_unitlogic_1 (.a_i(a_i), .b_i(b_i), .op_i(op_i), .f_o(alu_unitlogic_1_f_o));
  and and_5 (and_5_out, and_1_out, or_1_out);
  not not_4 (not_4_out, op_i[5]);
  and and_6 (and_6_out, overflow_o, not_4_out, not_5_out);
  not not_5 (not_5_out, op_i[4]);
  ALU_Selecteur alu_selecteur_1 (
    .r_o(alu_addsub_1_r_o), .cmp_o(alu_comp_1_cmp_o), .f_o(alu_unitlogic_1_f_o), .s_o(alu_custom_1_s_o),
    .op_i(op_i), .c_o(c_o));
  or or_2 (erreur_o, and_2_out, and_5_out, and_6_out);

  // Other names for the same wires on the sheet: op0_i = op_i[0]; op1_i = op_i[1]; op2_i = op_i[2]; op3_i = op_i[3];
  //   op4_i = op_i[4]; op5_i = op_i[5]

  // Notes on the sheet:
  //   Attention, votre version de Logisim
  //   ne contient pas de tracker. Si vous
  //   enregistrez votre projet, toutes les
  //   informations du tracker seront
  //   définitivement effacées.
endmodule

module ALU_AddSub (
  input  op3_i,
  input  [3:0] a_i,
  input  [3:0] b_i,
  input  op2_i,
  output zero_o,
  output [3:0] r_o,
  output Negative_o,
  output c_o,
  output overflow_o
);

  wire and_1_out, and_2_out, and_4_out, and_5_out, not_1_out, not_2_out, not_3_out, not_4_out, or_1_out,
       xor_5_out;
  wire [3:0] xor_1_out;

  not not_1 (not_1_out, a_i[3]);
  xor xor_1 (xor_1_out[0], op3_i, b_i[0]);
  xor xor_2 (xor_1_out[1], op3_i, b_i[1]);
  xor xor_3 (xor_1_out[2], op3_i, b_i[2]);
  xor xor_4 (xor_1_out[3], op3_i, b_i[3]);
  not not_2 (not_2_out, xor_1_out[3]);
  ALU_Add4Bit Add4Bit (.c_i(op3_i), .a_i(a_i), .b_i(xor_1_out), .r_o(r_o), .c_o(c_o));
  not not_3 (not_3_out, r_o[3]);
  and and_1 (and_1_out, not_3_out, a_i[3], xor_1_out[3]);
  and and_2 (and_2_out, r_o[3], not_2_out, not_1_out);
  nor nor_1 (zero_o, r_o[0], r_o[1], r_o[2], r_o[3]);
  not not_4 (not_4_out, op2_i);
  or or_1 (or_1_out, and_1_out, and_2_out);
  and and_3 (Negative_o, r_o[3], not_4_out);
  and and_4 (and_4_out, not_4_out, or_1_out);
  xor xor_5 (xor_5_out, op3_i, c_o);
  and and_5 (and_5_out, xor_5_out, op2_i);
  or or_2 (overflow_o, and_5_out, and_4_out);

  // Other names for the same wires on the sheet: r_o_bit3 = r_o[3]

  // Notes on the sheet:
  //   Attention, votre version de Logisim
  //   ne contient pas de tracker. Si vous
  //   enregistrez votre projet, toutes les
  //   informations du tracker seront
  //   définitivement effacées.
endmodule

module ALU_Add1Bit (
  input  a_i,
  input  b_i,
  input  c_i,
  output r_o,
  output c_o
);

  wire and_1_out, and_2_out, and_3_out, xor_1_out;

  xor xor_1 (xor_1_out, a_i, b_i);
  xor xor_2 (r_o, xor_1_out, c_i);
  and and_1 (and_1_out, a_i, b_i);
  and and_2 (and_2_out, a_i, c_i);
  and and_3 (and_3_out, b_i, c_i);
  or or_1 (c_o, and_1_out, and_2_out, and_3_out);

  // Notes on the sheet:
  //   Attention, votre version de Logisim
  //   ne contient pas de tracker. Si vous
  //   enregistrez votre projet, toutes les
  //   informations du tracker seront
  //   définitivement effacées.
endmodule

module ALU_Add4Bit (
  input  c_i,
  input  [3:0] a_i,
  input  [3:0] b_i,
  output [3:0] r_o,
  output c_o
);

  wire Add1BitA_c_o, Add1BitB_c_o, Add1BitC_c_o;

  ALU_Add1Bit Add1BitA (.a_i(a_i[0]), .b_i(b_i[0]), .c_i(c_i), .r_o(r_o[0]), .c_o(Add1BitA_c_o));
  ALU_Add1Bit Add1BitB (.a_i(a_i[1]), .b_i(b_i[1]), .c_i(Add1BitA_c_o), .r_o(r_o[1]), .c_o(Add1BitB_c_o));
  ALU_Add1Bit Add1BitC (.a_i(a_i[2]), .b_i(b_i[2]), .c_i(Add1BitB_c_o), .r_o(r_o[2]), .c_o(Add1BitC_c_o));
  ALU_Add1Bit Add1BitD (.a_i(a_i[3]), .b_i(b_i[3]), .c_i(Add1BitC_c_o), .r_o(r_o[3]), .c_o(c_o));

  // Notes on the sheet:
  //   Attention, votre version de Logisim
  //   ne contient pas de tracker. Si vous
  //   enregistrez votre projet, toutes les
  //   informations du tracker seront
  //   définitivement effacées.
endmodule

module ALU_Comp (
  input  Negative_i,
  input  carry_i,
  input  zero_i,
  input  [5:0] opcode_i,
  output [3:0] cmp_o
);

  wire not_1_out, not_2_out, not_3_out, xor_1_out;

  xor xor_1 (xor_1_out, Negative_i, carry_i);
  not not_1 (not_1_out, xor_1_out);
  not not_2 (not_2_out, zero_i);
  not not_3 (not_3_out, xor_1_out);
  Multiplexer #(.select(3), .enable("false")) multiplexer_1 (
    .in0(1'b0), .in1(not_1_out), .in2(xor_1_out), .in3(not_2_out), .in4(zero_i), .in5(xor_1_out),
    .in6(not_3_out), .in7(1'b0), .out(cmp_o[0]), .sel(opcode_i[2:0]));

  assign cmp_o[3:1] = 3'b000;

  // Notes on the sheet:
  //   Attention, votre version de Logisim
  //   ne contient pas de tracker. Si vous
  //   enregistrez votre projet, toutes les
  //   informations du tracker seront
  //   définitivement effacées.
endmodule

module ALU_UnitLogic (
  input  [3:0] a_i,
  input  [3:0] b_i,
  input  [5:0] op_i,
  output [3:0] f_o
);

  wire [3:0] and_1_out, not_1_out, or_1_out, xor_1_out;

  assign and_1_out = a_i & b_i;  // AND_Gate and_1, 4 bits wide
  assign or_1_out = a_i | b_i;  // OR_Gate or_1, 4 bits wide
  assign xor_1_out = a_i ^ b_i;  // XOR_Gate xor_1, 4 bits wide
  Multiplexer #(.select(2), .width(4), .enable("false")) multiplexer_1 (
    .in0(and_1_out), .in1(or_1_out), .in2(not_1_out), .in3(xor_1_out), .out(f_o), .sel(op_i[1:0]));
  assign not_1_out = ~and_1_out;  // NOT_Gate not_1, 4 bits wide

  // Notes on the sheet:
  //   Attention, votre version de Logisim
  //   ne contient pas de tracker. Si vous
  //   enregistrez votre projet, toutes les
  //   informations du tracker seront
  //   définitivement effacées.
endmodule

module ALU_Custom (
  input  [3:0] a_i,
  output [3:0] s_o
);

  wire [1:0] alu_add1bit_1_r_o, alu_add1bit_2_r_o;

  ALU_Add1Bit alu_add1bit_1 (
    .a_i(a_i[0]), .b_i(a_i[1]), .c_i(1'b0), .r_o(alu_add1bit_1_r_o[0]), .c_o(alu_add1bit_1_r_o[1]));
  ALU_Add1Bit alu_add1bit_2 (
    .a_i(a_i[2]), .b_i(a_i[3]), .c_i(1'b0), .r_o(alu_add1bit_2_r_o[0]), .c_o(alu_add1bit_2_r_o[1]));
  ALU_Add4Bit alu_add4bit_1 (
    .c_i(1'b0), .a_i({2'b00, alu_add1bit_1_r_o}), .b_i({2'b00, alu_add1bit_2_r_o}), .r_o(s_o));  // open: c_o

  // Notes on the sheet:
  //   Attention, votre version de Logisim
  //   ne contient pas de tracker. Si vous
  //   enregistrez votre projet, toutes les
  //   informations du tracker seront
  //   définitivement effacées.
endmodule

module ALU_Selecteur (
  input  [3:0] r_o,
  input  [3:0] cmp_o,
  input  [3:0] f_o,
  input  [3:0] s_o,
  input  [5:0] op_i,
  output [3:0] c_o
);

  Multiplexer #(.select(3), .width(4), .enable("false")) multiplexer_1 (
    .in0(r_o), .in1(r_o), .in2(4'b0000), .in3(cmp_o), .in4(f_o), .in5(f_o), .in6(s_o), .in7(s_o), .out(c_o),
    .sel(op_i[5:3]));

  // Notes on the sheet:
  //   Attention, votre version de Logisim
  //   ne contient pas de tracker. Si vous
  //   enregistrez votre projet, toutes les
  //   informations du tracker seront
  //   définitivement effacées.
endmodule
